// Logisim project task1_adder.circ as structural Verilog: 1 circuit, main circuit main
module main (
  input  [7:0] in_1,
  input  in_2,
  input  [7:0] in_3,
  output [7:0] out_4,
  output out_5
);

  wire and_1_out, and_2_out, and_3_out, and_4_out, and_5_out, and_6_out, and_7_out, and_8_out, and_9_out,
       and_10_out, and_11_out, and_12_out, and_13_out, and_14_out, and_15_out, and_16_out, or_1_out,
       or_2_out, or_3_out, or_4_out, or_5_out, or_6_out, or_7_out, or_8_out, xor_1_out, xor_2_out, xor_3_out,
       xor_4_out, xor_5_out, xor_6_out, xor_7_out, xor_8_out;

  // Probe on in_3
  // Probe on in_1
  xor xor_1 (xor_1_out, in_1[0], in_3[0]);
  xor xor_2 (xor_2_out, in_1[1], in_3[1]);
  xor xor_3 (xor_3_out, in_1[2], in_3[2]);
  xor xor_4 (xor_4_out, in_1[3], in_3[3]);
  xor xor_5 (xor_5_out, in_1[4], in_3[4]);
  xor xor_6 (xor_6_out, in_1[5], in_3[5]);
  xor xor_7 (xor_7_out, in_1[6], in_3[6]);
  xor xor_8 (xor_8_out, in_1[7], in_3[7]);
  and and_1 (and_1_out, xor_1_out, in_2);
  and and_2 (and_2_out, in_1[0], in_3[0]);
  and and_3 (and_3_out, xor_2_out, or_1_out);
  and and_4 (and_4_out, in_1[1], in_3[1]);
  and and_5 (and_5_out, xor_3_out, or_2_out);
  and and_6 (and_6_out, in_1[2], in_3[2]);
  and and_7 (and_7_out, xor_4_out, or_3_out);
  and and_8 (and_8_out, in_1[3], in_3[3]);
  and and_9 (and_9_out, xor_5_out, or_4_out);
  and and_10 (and_10_out, in_1[4], in_3[4]);
  and and_11 (and_11_out, xor_6_out, or_5_out);
  and and_12 (and_12_out, in_1[5], in_3[5]);
  and and_13 (and_13_out, xor_7_out, or_6_out);
  and and_14 (and_14_out, in_1[6], in_3[6]);
  and and_15 (and_15_out, xor_8_out, or_7_out);
  and and_16 (and_16_out, in_1[7], in_3[7]);
  xor xor_9 (out_4[0], xor_1_out, in_2);
  or or_1 (or_1_out, and_1_out, and_2_out);
  xor xor_10 (out_4[1], xor_2_out, or_1_out);
  or or_2 (or_2_out, and_3_out, and_4_out);
  xor xor_11 (out_4[2], xor_3_out, or_2_out);
  or or_3 (or_3_out, and_5_out, and_6_out);
  xor xor_12 (out_4[3], xor_4_out, or_3_out);
  or or_4 (or_4_out, and_7_out, and_8_out);
  xor xor_13 (out_4[4], xor_5_out, or_4_out);
  or or_5 (or_5_out, and_9_out, and_10_out);
  xor xor_14 (out_4[5], xor_6_out, or_5_out);
  or or_6 (or_6_out, and_11_out, and_12_out);
  xor xor_15 (out_4[6], xor_7_out, or_6_out);
  or or_7 (or_7_out, and_13_out, and_14_out);
  xor xor_16 (out_5, xor_8_out, or_7_out);
  or or_8 (or_8_out, and_15_out, and_16_out);
  // Probe on {in_2, out_4[6:0]}

  assign out_4[7] = in_2;
endmodule
