// Logisim project task2_grayBCD.circ as structural Verilog: 1 circuit, main circuit main
module main (
  input  A3,
  input  A2,
  input  A1,
  input  A0,
  input  B3,
  input  B2,
  input  B1,
  input  B0,
  output T3,
  output T2,
  output T1,
  output T0,
  output U3,
  output U2,
  output U1,
  output U0
);

  wire adder_1_cout, and_1_out, and_2_out, and_3_out, and_4_out, and_5_out, and_6_out, and_7_out, and_8_out,
       and_9_out, and_10_out, and_11_out, and_12_out, and_13_out, and_14_out, and_15_out, and_16_out,
       and_17_out, and_18_out, and_19_out, and_20_out, and_21_out, and_22_out, not_1_out, not_2_out,
       not_3_out, not_4_out, not_5_out;
  wire [2:0] xor_3_out, xor_6_out;
  wire [3:0] adder_1_out;

  xor xor_1 (xor_3_out[2], A3, A2);
  xor xor_2 (xor_3_out[1], xor_3_out[2], A1);
  xor xor_3 (xor_3_out[0], xor_3_out[1], A0);
  xor xor_4 (xor_6_out[2], B3, B2);
  xor xor_5 (xor_6_out[1], xor_6_out[2], B1);
  xor xor_6 (xor_6_out[0], xor_6_out[1], B0);
  // Probe on {A3, xor_3_out}
  // Probe on {B3, xor_6_out}
  Adder #(.width(4)) adder_1 (
    .a({A3, xor_3_out}), .b({B3, xor_6_out}), .out(adder_1_out), .cout(adder_1_cout));  // open: cin
  // Probe on adder_1_out
  // Probe on adder_1_cout
  not not_1 (not_1_out, adder_1_cout);
  not not_2 (not_2_out, adder_1_out[3]);
  not not_3 (not_3_out, adder_1_out[2]);
  not not_4 (not_4_out, adder_1_out[1]);
  not not_5 (not_5_out, adder_1_out[0]);
  and and_1 (and_1_out, adder_1_out[3], adder_1_out[1], adder_1_out[0]);
  and and_2 (and_2_out, adder_1_out[3], adder_1_out[2]);
  or or_1 (T0, adder_1_out[0], adder_1_out[1], adder_1_out[2], adder_1_out[3], adder_1_cout);
  and and_3 (and_3_out, adder_1_out[3], adder_1_out[2], adder_1_out[1]);
  and and_4 (and_4_out, not_1_out, not_2_out, adder_1_out[1]);
  and and_5 (and_5_out, not_5_out, not_4_out, not_3_out, not_2_out);
  and and_6 (and_6_out, not_1_out, not_3_out, adder_1_out[1], not_5_out);
  and and_7 (and_7_out, adder_1_cout, not_4_out);
  and and_8 (and_8_out, adder_1_cout, not_4_out, not_5_out);
  and and_9 (and_9_out, not_2_out, not_3_out, adder_1_out[1], adder_1_out[0]);
  and and_10 (and_10_out, adder_1_out[3], adder_1_out[2], adder_1_out[1]);
  and and_11 (and_11_out, not_2_out, adder_1_out[2], not_4_out);
  and and_12 (and_12_out, adder_1_out[2], adder_1_out[1], not_5_out);
  and and_13 (and_13_out, adder_1_out[3], adder_1_out[2], adder_1_out[0]);
  and and_14 (and_14_out, adder_1_out[2], adder_1_out[1], adder_1_out[0]);
  and and_15 (and_15_out, adder_1_out[3], not_3_out, not_4_out);
  and and_16 (and_16_out, not_2_out, adder_1_out[2], adder_1_out[0]);
  and and_17 (and_17_out, adder_1_out[3], not_3_out, not_5_out);
  and and_18 (and_18_out, not_3_out, not_4_out, not_5_out);
  and and_19 (and_19_out, not_2_out, adder_1_out[2], adder_1_out[1]);
  and and_20 (and_20_out, not_1_out, not_2_out, not_3_out, not_4_out, not_5_out);
  and and_21 (and_21_out, adder_1_out[3], not_3_out, not_4_out, adder_1_out[0]);
  and and_22 (and_22_out, adder_1_out[3], not_3_out, adder_1_out[1], not_5_out);
  or or_2 (T1, adder_1_cout, and_1_out, and_2_out);
  or or_3 (U0, and_3_out, and_4_out, and_5_out, and_6_out, and_7_out);
  or or_4 (U1, and_8_out, and_9_out, and_10_out, and_11_out, and_12_out, and_13_out);
  or or_5 (U2, adder_1_cout, and_14_out, and_15_out, and_16_out, and_17_out, and_18_out, and_19_out);
  or or_6 (U3, and_20_out, and_21_out, and_22_out);

  // Notes on the sheet:
  //   S3
  //   S4
  //   S1
  //   S2
  //   S0
endmodule
