// Logisim project task3_t_trigger.circ as structural Verilog: 1 circuit, main circuit main
module main (
  input  in_1,
  input  in_2,
  input  in_3,
  input  in_4,
  input  in_5,
  input  in_6,
  input  in_7,
  input  in_8,
  input  in_9,
  input  in_10,
  input  in_11,
  output out_12,
  output out_13,
  output out_14
);

  wire clock_1_out, d_ff_1_q, d_ff_1_qn, j_k_ff_1_q, j_k_ff_1_qn, nand_1_out, nand_2_out, s_r_ff_1_q,
       s_r_ff_1_qn, t_ff_1_q, t_ff_1_qn;

  S_R_Flip_Flop s_r_ff_1 (.S(in_2), .R(in_3), .clk(in_4), .Q(s_r_ff_1_q), .Qn(s_r_ff_1_qn));  // open: reset, preset
  D_Flip_Flop d_ff_1 (.D(in_5), .clk(in_6), .Q(d_ff_1_q), .Qn(d_ff_1_qn));  // open: preset, reset
  T_Flip_Flop t_ff_1 (.T(in_7), .clk(in_8), .Q(t_ff_1_q), .Qn(t_ff_1_qn));  // open: reset, preset
  J_K_Flip_Flop j_k_ff_1 (.J(in_9), .K(in_10), .clk(in_11), .Q(j_k_ff_1_q), .Qn(j_k_ff_1_qn));  // open: preset, reset
  T_Flip_Flop t_ff_2 (.T(in_1), .clk(clock_1_out), .Q(out_14));  // open: Qn, reset, preset
  Clock clock_1 (.out(clock_1_out));
  LED led_1 (.in(s_r_ff_1_q));
  LED led_2 (.in(s_r_ff_1_qn));
  LED led_3 (.in(d_ff_1_q));
  LED led_4 (.in(d_ff_1_qn));
  LED led_5 (.in(t_ff_1_q));
  LED led_6 (.in(t_ff_1_qn));
  LED led_7 (.in(j_k_ff_1_q));
  LED led_8 (.in(j_k_ff_1_qn));
  T_Flip_Flop t_ff_3 (.T(out_14), .clk(clock_1_out), .Q(out_13));  // open: Qn, reset, preset
  nand nand_1 (nand_1_out, out_14, out_13);
  nand nand_2 (nand_2_out, nand_1_out, nand_1_out);
  T_Flip_Flop t_ff_4 (.T(nand_2_out), .clk(clock_1_out), .Q(out_12));  // open: Qn, reset, preset
endmodule
